# Fritzing sketch fritzing (saved by Fritzing 0.9.3b)

parts:
  パーツ1 = CHIRIMEN
  S1 = Reed switch [package=THT]
  PIR1 = PIR sensor
  LED1 = smd LED [color="Red (633nm)" package="1206 [SMD]"]

nets:
  N1: パーツ1.CN2-5_ALOUT, パーツ1.CN1-9_SPI0_RX, S1.pin_1
  N2: パーツ1.CN2-6_AROUT, パーツ1.CN1-10_SPI0_TX, PIR1.SIG
  N3: パーツ1.CN1-1_GND, S1.pin_2
  N4: パーツ1.CN1-15_GND, PIR1.GND
  N5: パーツ1.CN1-17_VCC_3V3, PIR1.VDD
  N6: パーツ1.CN2-17_GND, LED1.cathode
  N7: パーツ1.CN2-13_UART0_TX, LED1.anode

custom parts:
  CHIRIMEN: CHIRIMEN board.
